# Fritzing sketch randomTest (saved by Fritzing 0.9.3b)
circuit board: 6.88566cm x 5.36311cm
breadboards: 1

parts:
  LED1 = LED - 5mm [color="White (4500K)" package="5 mm [THT]"]
  LED2 = LED - 5mm [color="White (4500K)" package="5 mm [THT]"]
  R1 = Resistor [tolerance=±5% resistance=220 package=THT]
  R2 = Resistor [tolerance=±5% resistance=220 package=THT]
  Bauteil1 = Arduino Uno (Rev3)

nets:
  N1: LED1.cathode, LED2.cathode, Bauteil1.GND
  N2: LED1.anode, R1.Pin_1
  N3: LED2.anode, R2.Pin_1
  N4: R1.Pin_0, Bauteil1.D10_PWM/SS
  N5: R2.Pin_0, Bauteil1.D9_PWM

notes:
  FLIP FLOP

// code stored in the sketch: FlipFlop.ino
/*
  Flip Flop
  switching between two LEDs using a button
  
  This example is part of the Fritzing Creator Kit: www.fritzing.org/creator-kit.
*/

int buttonPin=2;                       // Pin where the button is attached
int greenLED=9;                        // Pin where the green LED is attached
int redLED=10;                         // Pin where the red LED is attached 

void setup(){
  pinMode(buttonPin, INPUT);           // button is initialised as INPUT 
  pinMode(greenLED, OUTPUT);           // green LED pin is initialised as OUTPUT 
  pinMode(redLED, OUTPUT);             // red LED pin is initialised as OUTPUT  
}

void loop(){
  if (digitalRead(buttonPin)==LOW){    // if the button is pressed (LOW) 
    digitalWrite(greenLED, HIGH);      // switch on green LED
    digitalWrite(redLED, LOW);         // switch off red LED
  } else {                             // else (if button is not pressed)
    digitalWrite(greenLED, LOW);       // switch off green LED
    digitalWrite(redLED, HIGH);        // switch on red LED
  }
}

// code stored in the sketch: Workshop_06_Automatic-Lightning.ino
class Flasher
{
  // Class Member Variables
  // These are initialized at startup
  int ledPin;      // the number of the LED pin
  long OnTime;     // milliseconds of on-time
  long OffTime;    // milliseconds of off-time

  // These maintain the current state
  int ledState;                 // ledState used to set the LED
  unsigned long previousMillis;   // will store last time LED was updated

  // Constructor - creates a Flasher 
  // and initializes the member variables and state
  public:
  Flasher(int pin, long on, long off)
  {
  ledPin = pin;
  pinMode(ledPin, OUTPUT);     
    
  OnTime = on;
  OffTime = off;
  
  ledState = LOW; 
  previousMillis = 0;
  }

  void Update()
  {
    // check to see if it's time to change the state of the LED
    unsigned long currentMillis = millis();
     
    if((ledState == HIGH) && (currentMillis - previousMillis >= OnTime))
    {
      ledState = LOW;  // Turn it off
      previousMillis = currentMillis;  // Remember the time
      digitalWrite(ledPin, ledState);  // Update the actual LED
    }
    else if ((ledState == LOW) && (currentMillis - previousMillis >= OffTime))
    {
      ledState = HIGH;  // turn it on
      previousMillis = currentMillis;   // Remember the time
      digitalWrite(ledPin, ledState);   // Update the actual LED
    }
  }
};


Flasher led1(9, 100, 400);
Flasher led2(10, 350, 350);

void setup()
{
}

void loop()
{
  led1.Update();
  led2.Update();
}
